# Fritzing sketch RetroStick (saved by Fritzing 0.9.1b)
perfboards: 1

parts:
  J32 = shrouded pin header, 40 pins [form="♂ (shrouded male)"]
  J33 = double row male pin header, 4 pins [form="♂ (male)"]
  J34 = double row male pin header, 4 pins [form="♂ (male)"]
  MCP1 = MCP23017 [package="DIP (Dual Inline) [THT]"]
  IC5 = MCP23008 [chip_label=MCP23008 package="DIP (Dual Inline) [THT]"]
  J35 = double row male pin header, 4 pins [form="♂ (male)"]
  J36 = double row male pin header, 4 pins [form="♂ (male)"]
  J37 = double row male pin header, 4 pins [form="♂ (male)"]
  J38 = double row male pin header, 4 pins [form="♂ (male)"]
  Raspberry_Pi1 = Raspberry Pi B+  # not connected

nets:
  N1: J32.pin2, MCP1.SDA, IC5.SDA
  N2: J32.pin3, MCP1.SCL, IC5.SCL
  VSS: J32.pin5, MCP1.VSS, MCP1.A2, IC5.A2, IC5.A1, IC5.A0, IC5.Vss
  N3: J32.pin6, IC5.INT
  N4: J32.pin7, MCP1.INTB, MCP1.INTA
  VDD: J32.pin40, MCP1.VDD, MCP1.A0, MCP1.RESET, IC5.RESET, IC5.VDD
  N5: J33.pin1, IC5.GP0
  N6: J33.pin2, IC5.GP1
  N7: J33.pin3, IC5.GP2
  N8: J33.pin4, IC5.GP3
  N9: J34.pin1, IC5.GP4
  N10: J34.pin2, IC5.GP5
  N11: J34.pin3, IC5.GP6
  N12: J34.pin4, IC5.GP7
  N13: MCP1.GPB0, J37.pin4
  N14: MCP1.GPB1, J37.pin3
  N15: MCP1.GPB2, J37.pin2
  N16: MCP1.GPB3, J37.pin1
  N17: MCP1.GPB4, J38.pin4
  N18: MCP1.GPB5, J38.pin3
  N19: MCP1.GPB6, J38.pin2
  N20: MCP1.GPB7, J38.pin1
  N21: MCP1.GPBA0, J36.pin1
  N22: MCP1.GPBA1, J36.pin2
  N23: MCP1.GPBA2, J36.pin3
  N24: MCP1.GPBA3, J36.pin4
  N25: MCP1.GPBA4, J35.pin1
  N26: MCP1.GPBA5, J35.pin2
  N27: MCP1.GPBA6, J35.pin3
  N28: MCP1.GPBA7, J35.pin4

notes:
  COIN1
  COIN2
  RELAY FOR SCREEN
  KVM Switch ON
  KVM Switch Select

custom parts:
  MCP23017: Highspeed I2C 16-Bit Portexpander
  MCP23008: Highspeed 8-Bit Portexpander
